# Fritzing sketch Motor Test Sketch (saved by Fritzing 0.9.3b)
circuit board: 18.5cm x 8.63842cm
breadboards: 1

parts:
  U3 = atmega328 [package=dip]
  R17 = Resistor [tolerance=±5% resistance=10k package=THT]
  XTAL = Crystal [frequency="16 Mhz" package=THT]
  R15 = Resistor [tolerance=±5% resistance=1k package=THT]
  Q2 = NPN-Transistor [part_number=2N2222A package="TO92 [THT]"]
  C6 = Ceramic Capacitor [capacitance=22pF package="100 mil [THT, multilayer]"]
  C5 = Ceramic Capacitor [capacitance=22pF package="100 mil [THT, multilayer]"]
  - = screw terminal, 2 pins
  C7 = Ceramic Capacitor [capacitance="100 nF" package="100 mil [THT, multilayer]"]
  C10 = Electrolytic Capacitor [capacitance=33µF voltage=25V package="100 mil [THT, electrolytic]"]
  R14 = Resistor [tolerance=±5% resistance=1k package=THT]
  R16 = Resistor [tolerance=±5% resistance=1k package=THT]
  C9 = Ceramic Capacitor [capacitance="100 nF" package="100 mil [THT, multilayer]"]
  C8 = Ceramic Capacitor [capacitance="100 nF" package="100 mil [THT, multilayer]"]
  Q10 = MOSFET-NCHANNEL [package=sot23-3]
  R25 = Resistor [tolerance=±5% resistance=56k package=THT]
  R29 = Resistor [tolerance=±5% resistance=22k package=THT]
  R24 = Resistor [tolerance=±5% resistance=56k package=THT]
  R28 = Resistor [tolerance=±5% resistance=22k package=THT]
  SIM800L_20MM1 = SIM800L_20MM
  J48 = rounded female pin header, 2 pins [form="♀ (female rounded)"]
  RESET1 = Pushbutton [package="[THT]"]
  J60 = Rectifier_6A [package=THT]
  J72 = 4pth XH JST CUSTOM [form="♀ (female rounded)" package=THT]
  J77 = 2PTH JST FROM HEADER 5 [form="♀ (female rounded)" package=THT]
  C12 = Electrolytic Capacitor [capacitance=0.47mF voltage=10V package="200 mil [THT, electrolytic]"]
  D8 = Diode [package=diode-1n4001]
  R30 = Resistor [tolerance=±5% resistance=1k package=THT]
  C2 = Capacitor Polarized [package=cpol-radial-1000uf-25v]
  R32 = Resistor [tolerance=±5% resistance=1k package=THT]
  R33 = Resistor [tolerance=±5% resistance=2k package=THT]
  Q11 = Sharp PC817 [package=THT]
  Q12 = NPN-Transistor [part_number=2N2222A package="TO92 [THT]"]
  R34 = Resistor [tolerance=±5% resistance=1k package=THT]
  R35 = Resistor [tolerance=±5% resistance=1k package=THT]
  Q13 = Sharp PC817 [package=THT]
  Q14 = NPN-Transistor [part_number=2N2222A package="TO92 [THT]"]
  R36 = Resistor [tolerance=±5% resistance=1k package=THT]
  J78 = 3pth XH JST Custom [form="♀ (female rounded)" package=THT]
  J79 = rounded female pin header, 2 pins [form="♀ (female rounded)"]
  J81 = 4pth XH JST CUSTOM [form="♀ (female rounded)" package=THT]
  R37 = Resistor [tolerance=±5% resistance=1k package=THT]
  LED1 = LED - 3mm [color="Red (633nm)" package="3 mm [THT]"]
  D11 = Diode [package=diode-1n4148]
  RL3 = OMRON PCB Power Relay – G5LE [part_number="G5LE-1\n" package=THT]
  RL4 = OMRON PCB Power Relay – G5LE [part_number="G5LE-1\n" package=THT]
  C_START_STOP = screw terminal, 3 pins
  D12 = Diode [package=diode-1n4148]
  R_B = screw terminal, 2 pins
  R38 = Resistor [tolerance=±5% resistance=150k package=THT]
  R_Y_B = screw terminal, 3 pins
  R39 = Resistor [tolerance=±5% resistance=150k package=THT]
  R40 = Resistor [tolerance=±5% resistance=68k package=THT]
  R41 = Resistor [tolerance=±5% resistance=15k package=THT]
  R42 = Resistor [tolerance=±5% resistance=150k package=THT]
  C14 = Capacitor [part_number=0.047uF package=cap-pth-large]
  R43 = Resistor [tolerance=±5% resistance=150k package=THT]
  C15 = Capacitor [part_number=0.047uF package=cap-pth-large]
  J83 = 3pth XH JST Custom [form="♀ (female rounded)" package=THT]
  J84 = 3pth XH JST Custom [form="♀ (female rounded)" package=THT]
  Q17 = MOSFET-NCHANNEL [package=sot23-3]
  U9 = MOV [package=v18za2p]
  R48 = Resistor [tolerance=±5% resistance=22k package=THT]
  4V_Step_Down = MP1584 Step Down Module [part_number=MP1584]
  LM2596_Module4 = LM2596 Step Down Module
  S3 = Push Button Switch [package=os]
  D7 = Diode [package=diode-1n4001]
  D16 = Diode [package=diode-1n4001]
  D15 = Diode [package=diode-1n4001]
  D13 = Diode [package=diode-1n4001]
  D14 = Diode [package=diode-1n4001]
  R49 = Resistor [tolerance=±5% resistance=500 package=THT]
  Q18 = Sharp PC817 [package=THT]
  C16 = Capacitor Polarized [package=cpol-radial-100uf-25v]
  C17 = Ceramic Capacitor [capacitance="100 nF" package="100 mil [THT, multilayer]"]
  C18 = Ceramic Capacitor [capacitance="100 nF" package="100 mil [THT, multilayer]"]
  R54 = Resistor [tolerance=±5% resistance=10k package=THT]
  J85 = 3pth XH JST Custom [form="♀ (female rounded)" package=THT]
  R55 = Resistor [tolerance=±5% resistance=10k package=THT]
  R56 = Resistor [tolerance=±5% resistance=22k package=THT]
  R57 = Resistor [tolerance=±5% resistance=10k package=THT]
  M2 = LM339 [package="DIP (Dual Inline) [THT]"]
  D17 = Diode [part_number="2V7 Zener Diode" package=diode-1n4148]
  R58 = Resistor [tolerance=±5% resistance=1k package=THT]
  R59 = Resistor [tolerance=±5% resistance=1k package=THT]
  R60 = Resistor [tolerance=±5% resistance=1k package=THT]
  R61 = Resistor [tolerance=±5% resistance=1k package=THT]
  C19 = Electrolytic Capacitor [capacitance=33µF voltage=25V package="100 mil [THT, electrolytic]"]
  R62 = Resistor [tolerance=±5% resistance=1k package=THT]
  R63 = Resistor [tolerance=±5% resistance=500 package=THT]
  C20 = Ceramic Capacitor [capacitance="100 nF" package="100 mil [THT, multilayer]"]
  C21 = Ceramic Capacitor [capacitance="100 nF" package="100 mil [THT, multilayer]"]
  R64 = Resistor [tolerance=±5% resistance=1k package=THT]
  R66 = Resistor [tolerance=±5% resistance=1k package=THT]
  D9 = Diode [package=sma-diode]
  R67 = Resistor [tolerance=±5% resistance=10k package=THT]
  R68 = Resistor [tolerance=±5% resistance=22k package=THT]
  Q19 = NPN-Transistor [part_number=2N2222A package="TO92 [THT]"]
  R69 = Resistor [tolerance=±5% resistance=1k package=THT]
  RESET2 = Pushbutton [package="[THT]"]
  Charger = TP4056 W/O OUT
  R70 = Resistor [tolerance=±5% resistance=22k package=THT]
  J86 = 3pth XH JST Custom [form="♀ (female rounded)" package=THT]  # not connected
  J58 = rounded female pin header, 5 pins [form="♀ (female rounded)"]
  S4 = Push Button Switch [package=os]

nets:
  N1: U3.RESET, R17.Pin_1, RESET1.Pin_1, RESET1.Pin_2
  N2: U3.D0_(RX), J48.pin1
  N3: U3.D1_(TX), J48.pin2
  N4: U3.D2, R16.Pin_1
  N5: U3.D3_(PWM), R30.Pin_0
  N6: U3.D4, R15.Pin_1
  N7: U3.VCC, U3.AVCC, U3.AREF, R17.Pin_0, C7.1, C9.0, C8.1, SIM800L_20MM1.PIN2, C12.+, R32.Pin_1, Q17.D, R58.Pin_1, R59.Pin_1, R64.Pin_0, R66.Pin_1
  N8: U3.GND, Q2.E, C6.0, C5.1, C7.0, C10.-, C9.1, C8.0, SIM800L_20MM1.PIN_6, RESET1.Pin_3, RESET1.Pin_4, C12.-, Q12.E, Q14.E, R37.Pin_0, 4V_Step_Down.OUT-, C17.1, R62.Pin_0, J58.pin5
  N9: U3.XLAT1, XTAL.pin_0, C5.0
  N10: U3.XLAT2, XTAL.pin_1, C6.1
  N11: U3.D5_(PWM), J58.pin1
  N12: U3.D6_(PWM), J58.pin2
  N13: U3.D7, R68.Pin_0, J58.pin3
  N14: U3.D8, J58.pin4
  N15: U3.D9_(PWM), R63.Pin_1, C20.1
  N16: U3.D10_(PWM), R61.Pin_0, C19.+
  N17: U3.D11_(PWM), R14.Pin_0
  N18: U3.D13, Q13.Pin_2
  N19: U3.A0, Q11.Pin_2
  N20: U3.A2, J81.pin1
  N21: U3.A3, J81.pin2
  N22: U3.A4, J81.pin3
  N23: U3.A5, LED1.anode
  N24: R15.Pin_0, Q2.B
  N25: Q2.C, SIM800L_20MM1.PIN_8
  N26: -.pin1, Q10.D, Charger.B+
  N27: -.pin2, S4.NO1, S4.NO2
  N28: C10.+, R14.Pin_1, C17.0, J85.pin1
  N29: R16.Pin_0, SIM800L_20MM1.PIN_7
  N30: Q10.G, R54.Pin_0, R67.Pin_0
  N31: Q10.S, Q17.S, R54.Pin_1, D9.C, RESET2.Pin_3, RESET2.Pin_4
  N32: R25.Pin_0, R_B.pin2
  N33: R25.Pin_1, R29.Pin_0, U9.P$2
  N34: R29.Pin_1, Q18.Pin_1
  N35: R24.Pin_0, R_B.pin1
  N36: R24.Pin_1, U9.P$1, D7.C
  N37: R28.Pin_0, Q18.Pin_2
  N38: R28.Pin_1, D7.A
  N39: SIM800L_20MM1.PIN_4, J79.pin2
  N40: SIM800L_20MM1.PIN_5, J79.pin1
  N41: J60.DC_+, D8.A, C2.+
  N42: J60.AC_IN#1, J77.pin2
  N43: J60.AC_IN#2, J77.pin1
  N44: J60.DC_-, C2.-, S3.C1, S3.C2, S4.C1, S4.C2
  N45: J72.pin1, R48.Pin_0, D15.A, D14.A, Q18.Pin_3, C16.-
  N46: J72.pin2, R48.Pin_1, D16.C, D13.C, C16.+
  N47: J72.pin3, Q18.Pin_4
  N48: D8.C, 4V_Step_Down.IN+, LM2596_Module4.IN+, R55.Pin_0
  N49: R30.Pin_1, 4V_Step_Down.OUT+, D9.A, R69.Pin_1, RESET2.Pin_1
  N50: R32.Pin_0, R33.Pin_0, M2.+_Input_2
  N51: R33.Pin_1, R56.Pin_0, D17.A, R60.Pin_0, C19.-, R62.Pin_1, C20.0
  N52: Q11.Pin_1, Q13.Pin_1, R36.Pin_0
  N53: Q11.Pin_4, Q13.Pin_4, R36.Pin_1, J78.pin3, J81.pin4, M2.Vcc, C21.1, R64.Pin_1
  N54: Q11.Pin_3, R34.Pin_1
  N55: Q12.B, R34.Pin_0
  N56: Q12.C, J78.pin1
  N57: R35.Pin_0, Q13.Pin_3
  N58: R35.Pin_1, Q14.B
  N59: Q14.C, J78.pin2
  N60: R37.Pin_1, LED1.cathode
  N61: D11.A, RL4.COIL1, J83.pin2
  N62: D11.C, RL3.COIL1, RL4.COIL2, D12.C, J83.pin1
  N63: RL3.C, RL4.C, C_START_STOP.pin1
  N64: RL3.COIL2, D12.A, J83.pin3
  N65: RL3.B, C_START_STOP.pin3
  N66: RL4.A, C_START_STOP.pin2
  N67: R38.Pin_0, R_Y_B.pin1, J84.pin3
  N68: R38.Pin_1, R39.Pin_1, D16.A, D15.C
  N69: R_Y_B.pin2, R39.Pin_0, C14.2, J84.pin1
  N70: R_Y_B.pin3, R40.Pin_0
  N71: R40.Pin_1, R41.Pin_0
  N72: R41.Pin_1, R42.Pin_0
  N73: R42.Pin_1, R43.Pin_1, C15.1
  N74: C14.1, C15.2
  N75: R43.Pin_0, D13.A, D14.C
  N76: Q17.G, Q19.C
  N77: 4V_Step_Down.IN-, LM2596_Module4.OUT-, Charger.IN-
  N78: LM2596_Module4.IN-, S3.NO1, S3.NO2, C18.0, J85.pin3, R70.Pin_1
  N79: LM2596_Module4.OUT+, Charger.IN+
  N80: R49.Pin_0, C18.1, J85.pin2
  N81: R49.Pin_1, M2.-_Input_2
  N82: R55.Pin_1, R57.Pin_1, M2.+_Input_3
  N83: R56.Pin_1, M2.-_Input_3, R66.Pin_0
  N84: M2.Output_2, R61.Pin_1
  N85: M2.Output_1, R63.Pin_0
  N86: M2.-_Input_1, D17.C, R58.Pin_0
  N87: M2.+_Input_1, R59.Pin_0, R60.Pin_1
  N88: M2.Output_3, R67.Pin_1
  N89: R68.Pin_1, Q19.B, R69.Pin_0
  N90: Charger.B-, R70.Pin_0

notes:
  M-
  RX
  TX
  STX
  SRX
  1
  MOTOR
  FeedBack
  +
  Battery
  J1

custom parts:
  Rectifier_6A: stand Up rectifier 6A
  2PTH JST FROM HEADER 5: Generic rounded female header
  3pth XH JST Custom: 3PTH XH JST
  MOV: Metal Oxide Varistor
  MP1584 Step Down Module: Step Down Module based on MP1584
  LM2596 Step Down Module: LM2596 Step Down Regulator
  Push Button Switch: DPDT On/Off Switch, when pressed connects NO to C.
  LM339: LM339 Quad Comparator IC. DIP14 Package.
  TP4056 W/O OUT: A lithium battery charging and powering shield.
